# Fritzing sketch Wearable Compass (saved by Fritzing 0.9.3b)
breadboards: 1

parts:
  Part1 = 9-DOF Absolute Orientation IMU Fusion Breakout - BNO055  # not connected
  Part2 = Arduino Nano (Rev3.0)
  LED1 = LED - 5mm [color="Red (633nm)" package="5 mm [THT]"]
  Part3 = 9-DOF Absolute Orientation IMU Fusion Breakout - BNO055
  U1 = 74HC595 [package="DIP16 [THT]"]
  R1 = Resistor [tolerance=±5% resistance=220 package="2010 [SMD]"]
  LED2 = LED - 5mm [color="Red (633nm)" package="5 mm [THT]"]
  LED3 = LED - 5mm [color="Red (633nm)" package="5 mm [THT]"]
  LED4 = LED - 5mm [color="Red (633nm)" package="5 mm [THT]"]
  LED5 = LED - 5mm [color="Red (633nm)" package="5 mm [THT]"]
  LED6 = LED - 5mm [color="Red (633nm)" package="5 mm [THT]"]
  LED7 = LED - 5mm [color="Red (633nm)" package="5 mm [THT]"]
  LED8 = LED - 5mm [color="Red (633nm)" package="5 mm [THT]"]
  R2 = Resistor [tolerance=±5% resistance=220 package="2010 [SMD]"]
  R3 = Resistor [tolerance=±5% resistance=220 package="2010 [SMD]"]
  R4 = Resistor [tolerance=±5% resistance=220 package="2010 [SMD]"]
  R5 = Resistor [tolerance=±5% resistance=220 package="2010 [SMD]"]
  R6 = Resistor [tolerance=±5% resistance=220 package="2010 [SMD]"]
  R7 = Resistor [tolerance=±5% resistance=220 package="2010 [SMD]"]
  R8 = Resistor [tolerance=±5% resistance=220 package="2010 [SMD]"]

nets:
  GND: Part2.GND, Part3.GND, U1.GND
  N1: Part2.D3, U1.OE
  N2: Part2.D8, U1.ST_CP
  N3: Part2.D11/MOSI, U1.DS
  N4: Part2.D12/MISO, U1.SH_CP
  5V: Part2.5V, Part3.5.0V, U1.MR, U1.VCC
  N5: Part2.A5, Part3.SCL_5V
  N6: Part2.A4, Part3.SDA_5V
  N7: LED1.anode, R1.Pin_0
  N8: U1.Q1, R2.Pin_1
  N9: U1.Q2, R3.Pin_1
  N10: U1.Q3, R4.Pin_1
  N11: U1.Q4, R5.Pin_1
  N12: U1.Q5, R6.Pin_1
  N13: U1.Q6, R7.Pin_1
  N14: U1.Q7, R8.Pin_1
  N15: U1.Q0, R1.Pin_1
  N16: LED2.anode, R2.Pin_0
  N17: LED3.anode, R3.Pin_0
  N18: LED4.anode, R4.Pin_0
  N19: LED5.anode, R5.Pin_0
  N20: LED6.anode, R6.Pin_0
  N21: LED7.anode, R7.Pin_0
  N22: LED8.anode, R8.Pin_0

custom parts:
  9-DOF Absolute Orientation IMU Fusion Breakout - BNO055: A MEMS accelerometer, magnetometer and gyroscope on a single die with a high speed ARM Cortex-M0 based processor to digest all the sensor data, abstract the sensor fusion and real time requirements away, and spit out data you can use in quaternions, Euler angles or vectors.
